// Logisim project cpu.circ as structural Verilog: 1 circuit, main circuit cpu
module cpu (
  input  clk,
  input  [31:0] INSTRUCTION,
  input  [31:0] READ_DATA,
  output [31:0] WRITE_ADDRESS,
  output [31:0] PROGRAM_COUNTER,
  output [31:0] ra,
  output [31:0] sp,
  output [31:0] t0,
  output [31:0] t1,
  output [31:0] t2,
  output [31:0] s0,
  output [31:0] s1,
  output [31:0] a0,
  output [31:0] tohost,
  output [3:0] WRITE_ENABLE,
  output [31:0] WRITE_DATA
);

  wire ASel, BrEq, BrLt, BrUn, BSel, BSel1, MemRW, PCSel, RegWEn;
  wire [1:0] bit_extender_1_out, WBSel, WBSel1;
  wire [2:0] funct3, ImmSel;
  wire [3:0] ALUSel, ALUSel1;
  wire [3:1] undriven;
  wire [3:2] bit_extender_1_out_2, undriven_2;
  wire [4:0] rd1;
  wire [31:0] adder_1_out, adder_2_out, alu_res1, bit_extender_2_out, bit_extender_3_out, imm0, imm01, inst,
       multiplexer_1_out, multiplexer_2_out, multiplexer_3_out, multiplexer_4_out, pc, reg1, wb, wb1,
       wb_rdata;

  Adder #(.width(32)) adder_1 (.a(PROGRAM_COUNTER), .b(32'h4), .out(adder_1_out));  // open: cin, cout
  Register #(.width(5)) register_1 (.D(inst[11:7]), .en(1'b1), .clk(clk), .Q(rd1));  // open: clr
  Multiplexer #(.width(32)) multiplexer_1 (
    .in0(adder_1_out), .in1(WRITE_ADDRESS), .out(multiplexer_1_out), .sel(PCSel));
  Register #(.width(32)) u_PC (.D(multiplexer_1_out), .en(1'b1), .clk(clk), .Q(PROGRAM_COUNTER));  // open: clr
  Register #(.width(32)) register_2 (.D(wb), .en(1'b1), .clk(clk), .Q(wb1));  // open: clr
  Multiplexer #(.width(32)) multiplexer_2 (.in0(INSTRUCTION), .in1(32'h33), .out(multiplexer_2_out), .sel(PCSel));
  control_logic control_logic_1 (
    .inst({inst[31:15], funct3, inst[11:0]}), .BrEq(BrEq), .BrLt(BrLt), .PCSel(PCSel), .RegWEn(RegWEn),
    .ImmSel(ImmSel), .BrUn(BrUn), .ASel(ASel), .BSel(BSel), .ALUSel(ALUSel), .MemRW(MemRW), .WBSel(WBSel));  // open: CSRWen, CSRSel
  Register #(.width(32)) register_3 (.D(PROGRAM_COUNTER), .en(1'b1), .clk(clk), .Q(pc));  // open: clr
  Register #(.width(32)) register_4 (
    .D(multiplexer_2_out), .en(1'b1), .clk(clk), .Q({inst[31:15], funct3, inst[11:0]}));  // open: clr
  Register #(.width(32)) imm0val (.D(imm0), .en(1'b1), .clk(clk), .Q(imm01));  // open: clr
  Register #(.width(32)) register_5 (.D(WRITE_ADDRESS), .en(1'b1), .clk(clk), .Q(alu_res1));  // open: clr
  regfile regfile_1 (
    .rs1(inst[19:15]), .rs2(inst[24:20]), .rd(inst[11:7]), .Write_Data(wb), .RegWEn(RegWEn), .clk(clk),
    .ra(ra), .sp(sp), .t0(t0), .t1(t1), .t2(t2), .s0(s0), .s1(s1), .a0(a0), .Read_Data_1(reg1),
    .Read_Data_2(WRITE_DATA));
  Register #(.width(4)) register_6 (.D(ALUSel), .en(1'b1), .clk(clk), .Q(ALUSel1));  // open: clr
  imm_gen imm_gen_1 (.inst({inst[31:15], funct3, inst[11:0]}), .ImmSel(ImmSel), .imm(imm0));
  Multiplexer #(.width(32)) multiplexer_3 (.in0(reg1), .in1(pc), .out(multiplexer_3_out), .sel(ASel));
  Multiplexer #(.width(32)) multiplexer_4 (.in0(WRITE_DATA), .in1(imm0), .out(multiplexer_4_out), .sel(BSel));
  alu alu_1 (.A(multiplexer_3_out), .B(multiplexer_4_out), .ALUSel(ALUSel), .Result(WRITE_ADDRESS));
  Register #(.width(2)) register_7 (.D(WBSel), .en(1'b1), .clk(clk), .Q(WBSel1));  // open: clr
  Register #(.width(1)) register_8 (.D(BSel), .en(1'b1), .clk(clk), .Q(BSel1));  // open: clr
  branch_comp branch_comp_1 (.rs1(reg1), .rs2(WRITE_DATA), .BrUn(BrUn), .BrEq(BrEq), .BrLt(BrLt));
  Adder #(.width(32)) adder_2 (.a(pc), .b(32'h4), .out(adder_2_out));  // open: cin, cout
  Multiplexer #(.select(2), .width(32)) multiplexer_5 (
    .in0(WRITE_ADDRESS), .in1(wb_rdata), .in2(adder_2_out), .in3(adder_2_out), .out(wb), .sel(WBSel));
  csr csr_1 (.tohost(tohost));  // open: CSR_address, CSR_din, CSR_WE, clk
  assign {bit_extender_1_out_2, bit_extender_1_out} = {{3{MemRW}}, MemRW};  // Bit_Extender bit_extender_1
  assign bit_extender_2_out = {{24{READ_DATA[7]}}, READ_DATA[7:0]};  // Bit_Extender bit_extender_2
  assign bit_extender_3_out = {{16{READ_DATA[15]}}, READ_DATA[15:0]};  // Bit_Extender bit_extender_3
  Multiplexer #(.select(2), .width(4)) multiplexer_6 (
    .in0({undriven, bit_extender_1_out[0]}), .in1({undriven_2, bit_extender_1_out}),
    .in2({bit_extender_1_out_2, bit_extender_1_out}), .out(WRITE_ENABLE), .sel(funct3[1:0]));  // open: in3
  Multiplexer #(.select(2), .width(32)) multiplexer_7 (
    .in0(bit_extender_2_out), .in1(bit_extender_3_out), .in2(READ_DATA), .out(wb_rdata), .sel(funct3[1:0]));  // open: in3

  // Other names for the same wires on the sheet: alu_res[31:0] = WRITE_ADDRESS; opcode[6:0] = inst[6:0];
  //   rd[4:0] = inst[11:7]; inst[14:12] = funct3; rs1[4:0] = inst[19:15]; rs2[4:0] = inst[24:20];
  //   reg2[31:0] = WRITE_DATA

  // Notes on the sheet:
  //   Output to IMEM
  //   IMEM (do **NOT** move this)
  //   Inputs from IMEM
  //   Inputs/Outputs for testing. Do **NOT** move these.
  //   Outputs To DMEM
  //   DMEM (do **NOT** move this)
  //   Inputs From DMEM
endmodule
